// Logisim project alu.circ as structural Verilog: 1 circuit, main circuit alu
module alu (
  input  [31:0] A,
  input  [31:0] B,
  input  [3:0] ALUSel,
  output [31:0] ALUResult
);

  wire comparator_1_lt;
  wire [31:0] add0, AND7, MUL8, MULH9, MULHU11, multiplier_2_out, multiplier_3_out, OR6, SLL1, SLT2, SRA13,
       SRL5, SUB12, XOR4;
  wire [63:0] bit_extender_1_out, bit_extender_2_out, bit_extender_3_out, bit_extender_4_out;

  Shifter #(.width(32)) shifter_1 (.in(A), .\dist (B[4:0]), .out(SLL1));
  Comparator #(.width(32)) comparator_1 (.a(A), .b(B), .lt(comparator_1_lt));  // open: gt, eq
  assign XOR4 = A ^ B;  // XOR_Gate xor_1, 32 bits wide
  Shifter #(.shift("lr"), .width(32)) shifter_2 (.in(A), .\dist (B[4:0]), .out(SRL5));
  assign OR6 = A | B;  // OR_Gate or_1, 32 bits wide
  assign AND7 = A & B;  // AND_Gate and_1, 32 bits wide
  Multiplier #(.mode("twosComplement"), .width(32)) multiplier_1 (.a(A), .b(B), .out(MUL8));  // open: cin, cout
  assign bit_extender_1_out = {{32{A[31]}}, A};  // Bit_Extender bit_extender_1
  assign bit_extender_2_out = {{32{B[31]}}, B};  // Bit_Extender bit_extender_2
  assign bit_extender_3_out = {{32{1'b0}}, A};  // Bit_Extender bit_extender_3
  assign bit_extender_4_out = {{32{1'b0}}, B};  // Bit_Extender bit_extender_4
  Subtractor #(.width(32)) subtractor_1 (.a(A), .b(B), .out(SUB12));  // open: bin, bout
  Shifter #(.shift("ar"), .width(32)) shifter_3 (.in(A), .\dist (B[4:0]), .out(SRA13));
  Adder #(.width(32)) adder_1 (.a(A), .b(B), .out(add0));  // open: cin, cout
  assign SLT2 = {{31{1'b0}}, comparator_1_lt};  // Bit_Extender bit_extender_5
  Multiplier #(.mode("twosComplement"), .width(64)) multiplier_2 (
    .a(bit_extender_1_out), .b(bit_extender_2_out), .out({MULH9, multiplier_2_out}));  // open: cin, cout
  Multiplier #(.width(64)) multiplier_3 (
    .a(bit_extender_3_out), .b(bit_extender_4_out), .out({MULHU11, multiplier_3_out}));  // open: cin, cout
  Multiplexer #(.select(4), .width(32)) multiplexer_1 (
    .in0(add0), .in1(SLL1), .in2(SLT2), .in3(add0), .in4(XOR4), .in5(SRL5), .in6(OR6), .in7(AND7),
    .in8(MUL8), .in9(MULH9), .in10(add0), .in11(MULHU11), .in12(SUB12), .in13(SRA13), .in14(add0), .in15(B),
    .out(ALUResult), .sel(ALUSel));

  // Other names for the same wires on the sheet: s0 = ALUSel[0]; s1 = ALUSel[1]; s2 = ALUSel[2]; s3 = ALUSel[3]

  // Notes on the sheet:
  //   INPUTS to your circuit
  //   DON'T CHANGE THE LOCATIONS OF THE INPUTS AND OUTPUTS!
  //   OUTPUT from your circuit
endmodule
