// Logisim project cpu.circ as structural Verilog: 1 circuit, main circuit cpu
module cpu (
  input  clk,
  input  [31:0] Instruction,
  input  [31:0] MemReadData,
  output [31:0] MemAddress,
  output [31:0] ProgramCounter,
  output [31:0] ra,
  output [31:0] sp,
  output [31:0] t0,
  output [31:0] t1,
  output [31:0] t2,
  output [31:0] s0,
  output [31:0] s1,
  output [31:0] a0,
  output [3:0] MemWriteMask,
  output [31:0] MemWriteData
);

  wire ASel, BrEq, BrLt, BrUn, BSel, MemWEn, PCSel, RegWEn;
  wire [1:0] WBSel;
  wire [2:0] ImmSel;
  wire [3:0] ALUSel;
  wire [31:0] A, B, DMem_Result, IMM, Instruction_t, multiplexer_1_out, multiplexer_2_out, PC4, pcbooger,
       Read1, Read2, register_3_q, Result;

  Adder #(.width(32)) adder_1 (.a(ProgramCounter), .b(32'h4), .out(pcbooger));  // open: cin, cout
  Register #(.width(32)) register_1 (.D(pcbooger), .clk(clk), .Q(PC4));  // open: en, clr
  Multiplexer #(.width(32)) multiplexer_1 (.in0(Instruction), .in1(32'h13), .out(multiplexer_1_out), .sel(PCSel));
  Multiplexer #(.width(32)) multiplexer_2 (.in0(pcbooger), .in1(MemAddress), .out(multiplexer_2_out), .sel(PCSel));
  Register #(.width(32)) register_2 (.D(multiplexer_1_out), .clk(clk), .Q(Instruction_t));  // open: en, clr
  Register #(.width(32)) PC (.D(multiplexer_2_out), .clk(clk), .Q(ProgramCounter));  // open: en, clr
  Multiplexer #(.select(2), .width(32)) multiplexer_3 (
    .in0(DMem_Result), .in1(MemAddress), .in2(PC4), .out(Result), .sel(WBSel));  // open: in3
  // Probe on PCSel
  // Probe on ImmSel
  control_logic control_logic_1 (
    .Instruction(Instruction_t), .BrEq(BrEq), .BrLt(BrLt), .PCSel(PCSel), .RegWEn(RegWEn), .ImmSel(ImmSel),
    .BrUn(BrUn), .ASel(ASel), .BSel(BSel), .ALUSel(ALUSel), .MemWEn(MemWEn), .WBSel(WBSel));
  regfile regfile_1 (
    .ReadIndex1(Instruction_t[19:15]), .ReadIndex2(Instruction_t[24:20]), .WriteIndex(Instruction_t[11:7]),
    .WriteData(Result), .RegWEn(RegWEn), .clk(clk), .ra(ra), .sp(sp), .t0(t0), .t1(t1), .t2(t2), .s0(s0),
    .s1(s1), .a0(a0), .ReadData1(Read1), .ReadData2(Read2));
  imm_gen imm_gen_1 (.Instruction(Instruction_t), .ImmSel(ImmSel), .Immediate(IMM));
  Register #(.width(32)) register_3 (.D(ProgramCounter), .clk(clk), .Q(register_3_q));  // open: en, clr
  Multiplexer #(.width(32)) multiplexer_4 (.in0(Read2), .in1(IMM), .out(B), .sel(BSel));
  Multiplexer #(.width(32)) multiplexer_5 (.in0(Read1), .in1(register_3_q), .out(A), .sel(ASel));
  // Probe on WBSel
  alu alu_1 (.A(A), .B(B), .ALUSel(ALUSel), .ALUResult(MemAddress));
  branch_comp branch_comp_1 (.BrData1(Read1), .BrData2(Read2), .BrUn(BrUn), .BrEq(BrEq), .BrLt(BrLt));
  partial_store partial_store_1 (
    .Instruction(Instruction_t), .MemAddress(MemAddress), .DataFromReg(Read2), .MemWEn(MemWEn),
    .MemWriteMask(MemWriteMask), .DataToMem(MemWriteData));
  partial_load partial_load_1 (
    .Instruction(Instruction_t), .MemAddress(MemAddress), .DataFromMem(MemReadData), .DataToReg(DMem_Result));

  // Other names for the same wires on the sheet: ALU_Result[31:0] = MemAddress; booger[31:0] = Instruction;
  //   opcode[6:0] = Instruction_t[6:0]; rd[4:0] = Instruction_t[11:7]; rs1[4:0] = Instruction_t[19:15];
  //   rs2[4:0] = Instruction_t[24:20]

  // Notes on the sheet:
  //   To IMEM
  //   IMEM (do **NOT** move this)
  //   From IMEM
  //   Inputs/Outputs for testing. Do **NOT** move these.
  //   It is OK to move the PC, RegFile, ALU, MEM, Branch Comp, Imm Gen, Partial Load, Partial Store and Control Logic to wherever is most convenient for you when constructing your CPU, and to delete this text
  //   To DMEM
  //   DMEM (do **NOT** move this)
  //   From DMEM
endmodule
