// Logisim project partial-load.circ as structural Verilog: 1 circuit, main circuit partial_load
module partial_load (
  input  [31:0] Instruction,
  input  [31:0] MemAddress,
  input  [31:0] DataFromMem,
  output [31:0] DataToReg
);

  wire comparator_1_eq, comparator_2_eq, comparator_3_eq, comparator_4_eq, comparator_5_eq, comparator_6_eq,
       comparator_7_eq;
  wire [1:0] bhw, Bits;
  wire [7:0] multiplexer_1_out;
  wire [15:0] multiplexer_2_out;
  wire [31:0] bit_extender_1_out, bit_extender_2_out;

  Comparator #(.width(10)) comparator_1 (
    .a(10'h3), .b({Instruction[14:12], Instruction[6:0]}), .eq(comparator_1_eq));  // open: gt, lt
  Comparator #(.width(10)) comparator_2 (
    .a({Instruction[14:12], Instruction[6:0]}), .b(10'h83), .eq(comparator_2_eq));  // open: gt, lt
  Comparator #(.width(10)) comparator_3 (
    .a({Instruction[14:12], Instruction[6:0]}), .b(10'h103), .eq(comparator_3_eq));  // open: gt, lt
  Comparator #(.width(2)) comparator_4 (.a(2'b00), .b(MemAddress[1:0]), .eq(comparator_4_eq));  // open: gt, lt
  Comparator #(.width(2)) comparator_5 (.a(MemAddress[1:0]), .b(2'b01), .eq(comparator_5_eq));  // open: gt, lt
  Comparator #(.width(2)) comparator_6 (.a(MemAddress[1:0]), .b(2'b10), .eq(comparator_6_eq));  // open: gt, lt
  Comparator #(.width(2)) comparator_7 (.a(MemAddress[1:0]), .b(2'b11), .eq(comparator_7_eq));  // open: gt, lt
  Priority_Encoder #(.select_enc(2)) priority_encoder_1 (
    .in0(1'b1), .in1(comparator_1_eq), .in2(comparator_2_eq), .in3(comparator_3_eq), .out(bhw));  // open: gs, en_out, en_in
  Priority_Encoder #(.select_enc(2)) priority_encoder_2 (
    .in0(comparator_4_eq), .in1(comparator_5_eq), .in2(comparator_6_eq), .in3(comparator_7_eq), .out(Bits));  // open: gs, en_out, en_in
  Multiplexer #(.select(2), .width(8)) multiplexer_1 (
    .in0(DataFromMem[7:0]), .in1(DataFromMem[15:8]), .in2(DataFromMem[23:16]), .in3(DataFromMem[31:24]),
    .out(multiplexer_1_out), .sel(Bits));
  Multiplexer #(.select(2), .width(16)) multiplexer_2 (
    .in0(DataFromMem[15:0]), .in1(DataFromMem[23:8]), .in2(DataFromMem[31:16]), .out(multiplexer_2_out),
    .sel(Bits));  // open: in3
  assign bit_extender_1_out = {{24{multiplexer_1_out[7]}}, multiplexer_1_out};  // Bit_Extender bit_extender_1
  assign bit_extender_2_out = {{16{multiplexer_2_out[15]}}, multiplexer_2_out};  // Bit_Extender bit_extender_2
  Multiplexer #(.select(2), .width(32)) multiplexer_3 (
    .in0(DataFromMem), .in1(bit_extender_1_out), .in2(bit_extender_2_out), .in3(DataFromMem),
    .out(DataToReg), .sel(bhw));

  // Other names for the same wires on the sheet: B1[7:0] = DataFromMem[7:0]; B2[7:0] = DataFromMem[15:8];
  //   B3[7:0] = DataFromMem[23:16]; B4[7:0] = DataFromMem[31:24];
  //   OpFunc3[9:0] = {Instruction[14:12], Instruction[6:0]}; Mb[1:0] = MemAddress[1:0]

  // Notes on the sheet:
  //   INPUTS to your circuit
  //   DON'T CHANGE THE LOCATIONS OF THE INPUTS AND OUTPUTS!
  //   OUTPUT from your circuit
endmodule
