// Logisim project partial-store.circ as structural Verilog: 1 circuit, main circuit partial_store
module partial_store (
  input  [31:0] Instruction,
  input  [31:0] MemAddress,
  input  [31:0] DataFromReg,
  input  MemWEn,
  output [3:0] MemWriteMask,
  output [31:0] DataToMem
);

  wire comparator_1_eq, comparator_2_eq, comparator_3_eq, comparator_4_eq, comparator_5_eq, comparator_6_eq,
       comparator_7_eq;
  wire [2:0] priority_encoder_1_out;
  wire [3:0] multiplexer_2_out;
  wire [31:0] bit_extender_1_out, bit_extender_2_out, bit_extender_3_out, bit_extender_4_out,
       bit_extender_5_out, bit_extender_6_out, shifter_1_out, shifter_2_out, shifter_3_out, shifter_4_out;

  Comparator #(.width(12)) comparator_1 (
    .a({MemAddress[1:0], Instruction[14:12], Instruction[6:0]}), .b(12'h23), .eq(comparator_1_eq));  // open: gt, lt
  Comparator #(.width(12)) comparator_2 (
    .a({MemAddress[1:0], Instruction[14:12], Instruction[6:0]}), .b(12'h423), .eq(comparator_2_eq));  // open: gt, lt
  Comparator #(.width(12)) comparator_3 (
    .a({MemAddress[1:0], Instruction[14:12], Instruction[6:0]}), .b(12'h823), .eq(comparator_3_eq));  // open: gt, lt
  Comparator #(.width(12)) comparator_4 (
    .a({MemAddress[1:0], Instruction[14:12], Instruction[6:0]}), .b(12'hc23), .eq(comparator_4_eq));  // open: gt, lt
  Comparator #(.width(12)) comparator_5 (
    .a({MemAddress[1:0], Instruction[14:12], Instruction[6:0]}), .b(12'ha3), .eq(comparator_5_eq));  // open: gt, lt
  Comparator #(.width(12)) comparator_6 (
    .a({MemAddress[1:0], Instruction[14:12], Instruction[6:0]}), .b(12'h8a3), .eq(comparator_6_eq));  // open: gt, lt
  Comparator #(.width(12)) comparator_7 (
    .a({MemAddress[1:0], Instruction[14:12], Instruction[6:0]}), .b(12'h123), .eq(comparator_7_eq));  // open: gt, lt
  Priority_Encoder priority_encoder_1 (
    .in0(1'b1), .in1(comparator_1_eq), .in2(comparator_2_eq), .in3(comparator_3_eq), .in4(comparator_4_eq),
    .in5(comparator_5_eq), .in6(comparator_6_eq), .in7(comparator_7_eq), .out(priority_encoder_1_out));  // open: en_in, gs, en_out
  assign bit_extender_1_out = {{24{1'b0}}, DataFromReg[7:0]};  // Bit_Extender bit_extender_1
  assign bit_extender_2_out = {{24{1'b0}}, DataFromReg[7:0]};  // Bit_Extender bit_extender_2
  assign bit_extender_3_out = {{24{1'b0}}, DataFromReg[7:0]};  // Bit_Extender bit_extender_3
  assign bit_extender_4_out = {{24{1'b0}}, DataFromReg[7:0]};  // Bit_Extender bit_extender_4
  assign bit_extender_5_out = {{16{1'b0}}, DataFromReg[15:0]};  // Bit_Extender bit_extender_5
  assign bit_extender_6_out = {{16{1'b0}}, DataFromReg[15:0]};  // Bit_Extender bit_extender_6
  Shifter #(.width(32)) shifter_1 (.in(bit_extender_2_out), .\dist (5'b01000), .out(shifter_1_out));
  Shifter #(.width(32)) shifter_2 (.in(bit_extender_3_out), .\dist (5'b10000), .out(shifter_2_out));
  Shifter #(.width(32)) shifter_3 (.in(bit_extender_4_out), .\dist (5'b11000), .out(shifter_3_out));
  Shifter #(.width(32)) shifter_4 (.in(bit_extender_6_out), .\dist (5'b10000), .out(shifter_4_out));
  Multiplexer #(.enable("true"), .select(3), .width(32)) multiplexer_1 (
    .in1(bit_extender_1_out), .in2(shifter_1_out), .in3(shifter_2_out), .in4(shifter_3_out),
    .in5(bit_extender_5_out), .in6(shifter_4_out), .in7(DataFromReg), .out(DataToMem),
    .sel(priority_encoder_1_out), .en(MemWEn));  // open: in0
  Multiplexer #(.enable("true"), .select(3), .width(4)) multiplexer_2 (
    .in1(4'b0001), .in2(4'b0010), .in3(4'b0100), .in4(4'b1000), .in5(4'b0011), .in6(4'b1100), .in7(4'b1111),
    .out(multiplexer_2_out), .sel(priority_encoder_1_out), .en(MemWEn));  // open: in0
  Multiplexer #(.width(4)) multiplexer_3 (.in0(4'b0000), .in1(multiplexer_2_out), .out(MemWriteMask), .sel(MemWEn));

  // Other names for the same wires on the sheet: B1[7:0] = DataFromReg[7:0]; B2[7:0] = DataFromReg[15:8];
  //   B3[7:0] = DataFromReg[23:16]; B4[7:0] = DataFromReg[31:24]; Mb[1:0] = MemAddress[1:0]

  // Notes on the sheet:
  //   INPUTS to your circuit
  //   DON'T CHANGE THE LOCATIONS OF THE INPUTS AND OUTPUTS!
  //   OUTPUT from your circuit
endmodule
