// Logisim project regfile.circ as structural Verilog: 1 circuit, main circuit regfile
module regfile (
  input  [4:0] ReadIndex1,
  input  [4:0] ReadIndex2,
  input  [4:0] WriteIndex,
  input  [31:0] WriteData,
  input  RegWEn,
  input  clk,
  output [31:0] ra,
  output [31:0] sp,
  output [31:0] t0,
  output [31:0] t1,
  output [31:0] t2,
  output [31:0] s0,
  output [31:0] s1,
  output [31:0] a0,
  output [31:0] ReadData1,
  output [31:0] ReadData2
);

  wire [31:0] a1, a2, a3, a4, a5, a6, a7, gp, multiplexer_1_out, multiplexer_2_out, multiplexer_3_out,
       multiplexer_4_out, multiplexer_5_out, multiplexer_6_out, multiplexer_7_out, multiplexer_8_out,
       multiplexer_11_out, multiplexer_12_out, multiplexer_13_out, multiplexer_14_out, multiplexer_15_out,
       multiplexer_16_out, multiplexer_17_out, multiplexer_18_out, multiplexer_19_out, multiplexer_20_out,
       multiplexer_21_out, multiplexer_22_out, multiplexer_23_out, multiplexer_24_out, multiplexer_25_out,
       multiplexer_26_out, multiplexer_27_out, multiplexer_28_out, multiplexer_29_out, multiplexer_30_out,
       multiplexer_31_out, multiplexer_32_out, multiplexer_33_out, s2, s3, s4, s5, s6, s7, s8, s9, s10, s11,
       t3, t4, t5, t6, tp;

  Multiplexer #(.select(5), .width(32)) multiplexer_1 (
    .in0(ra), .in1(WriteData), .in2(ra), .in3(ra), .in4(ra), .in5(ra), .in6(ra), .in7(ra), .in8(ra),
    .in9(ra), .in10(ra), .in11(ra), .in12(ra), .in13(ra), .in14(ra), .in15(ra), .in16(ra), .in17(ra),
    .in18(ra), .in19(ra), .in20(ra), .in21(ra), .in22(ra), .in23(ra), .in24(ra), .in25(ra), .in26(ra),
    .in27(ra), .in28(ra), .in29(ra), .in30(ra), .in31(ra), .out(multiplexer_1_out), .sel(WriteIndex));
  Register #(.width(32)) register_1 (.D(multiplexer_1_out), .en(RegWEn), .clk(clk), .Q(ra));  // open: clr
  Multiplexer #(.select(5), .width(32)) multiplexer_2 (
    .in0(sp), .in1(sp), .in2(WriteData), .in3(sp), .in4(sp), .in5(sp), .in6(sp), .in7(sp), .in8(sp),
    .in9(sp), .in10(sp), .in11(sp), .in12(sp), .in13(sp), .in14(sp), .in15(sp), .in16(sp), .in17(sp),
    .in18(sp), .in19(sp), .in20(sp), .in21(sp), .in22(sp), .in23(sp), .in24(sp), .in25(sp), .in26(sp),
    .in27(sp), .in28(sp), .in29(sp), .in30(sp), .in31(sp), .out(multiplexer_2_out), .sel(WriteIndex));
  Multiplexer #(.select(5), .width(32)) multiplexer_3 (
    .in0(t0), .in1(t0), .in2(t0), .in3(t0), .in4(t0), .in5(WriteData), .in6(t0), .in7(t0), .in8(t0),
    .in9(t0), .in10(t0), .in11(t0), .in12(t0), .in13(t0), .in14(t0), .in15(t0), .in16(t0), .in17(t0),
    .in18(t0), .in19(t0), .in20(t0), .in21(t0), .in22(t0), .in23(t0), .in24(t0), .in25(t0), .in26(t0),
    .in27(t0), .in28(t0), .in29(t0), .in30(t0), .in31(t0), .out(multiplexer_3_out), .sel(WriteIndex));
  Multiplexer #(.select(5), .width(32)) multiplexer_4 (
    .in0(t1), .in1(t1), .in2(t1), .in3(t1), .in4(t1), .in5(t1), .in6(WriteData), .in7(t1), .in8(t1),
    .in9(t1), .in10(t1), .in11(t1), .in12(t1), .in13(t1), .in14(t1), .in15(t1), .in16(t1), .in17(t1),
    .in18(t1), .in19(t1), .in20(t1), .in21(t1), .in22(t1), .in23(t1), .in24(t1), .in25(t1), .in26(t1),
    .in27(t1), .in28(t1), .in29(t1), .in30(t1), .in31(t1), .out(multiplexer_4_out), .sel(WriteIndex));
  Multiplexer #(.select(5), .width(32)) multiplexer_5 (
    .in0(t2), .in1(t2), .in2(t2), .in3(t2), .in4(t2), .in5(t2), .in6(t2), .in7(WriteData), .in8(t2),
    .in9(t2), .in10(t2), .in11(t2), .in12(t2), .in13(t2), .in14(t2), .in15(t2), .in16(t2), .in17(t2),
    .in18(t2), .in19(t2), .in20(t2), .in21(t2), .in22(t2), .in23(t2), .in24(t2), .in25(t2), .in26(t2),
    .in27(t2), .in28(t2), .in29(t2), .in30(t2), .in31(t2), .out(multiplexer_5_out), .sel(WriteIndex));
  Register #(.width(32)) register_2 (.D(multiplexer_2_out), .en(RegWEn), .clk(clk), .Q(sp));  // open: clr
  Register #(.width(32)) register_3 (.D(multiplexer_3_out), .en(RegWEn), .clk(clk), .Q(t0));  // open: clr
  Register #(.width(32)) register_4 (.D(multiplexer_4_out), .en(RegWEn), .clk(clk), .Q(t1));  // open: clr
  Register #(.width(32)) register_5 (.D(multiplexer_5_out), .en(RegWEn), .clk(clk), .Q(t2));  // open: clr
  Multiplexer #(.select(5), .width(32)) multiplexer_6 (
    .in0(s0), .in1(s0), .in2(s0), .in3(s0), .in4(s0), .in5(s0), .in6(s0), .in7(s0), .in8(WriteData),
    .in9(s0), .in10(s0), .in11(s0), .in12(s0), .in13(s0), .in14(s0), .in15(s0), .in16(s0), .in17(s0),
    .in18(s0), .in19(s0), .in20(s0), .in21(s0), .in22(s0), .in23(s0), .in24(s0), .in25(s0), .in26(s0),
    .in27(s0), .in28(s0), .in29(s0), .in30(s0), .in31(s0), .out(multiplexer_6_out), .sel(WriteIndex));
  Multiplexer #(.select(5), .width(32)) multiplexer_7 (
    .in0(s1), .in1(s1), .in2(s1), .in3(s1), .in4(s1), .in5(s1), .in6(s1), .in7(s1), .in8(s1),
    .in9(WriteData), .in10(s1), .in11(s1), .in12(s1), .in13(s1), .in14(s1), .in15(s1), .in16(s1), .in17(s1),
    .in18(s1), .in19(s1), .in20(s1), .in21(s1), .in22(s1), .in23(s1), .in24(s1), .in25(s1), .in26(s1),
    .in27(s1), .in28(s1), .in29(s1), .in30(s1), .in31(s1), .out(multiplexer_7_out), .sel(WriteIndex));
  Multiplexer #(.select(5), .width(32)) multiplexer_8 (
    .in0(a0), .in1(a0), .in2(a0), .in3(a0), .in4(a0), .in5(a0), .in6(a0), .in7(a0), .in8(a0), .in9(a0),
    .in10(WriteData), .in11(a0), .in12(a0), .in13(a0), .in14(a0), .in15(a0), .in16(a0), .in17(a0), .in18(a0),
    .in19(a0), .in20(a0), .in21(a0), .in22(a0), .in23(a0), .in24(a0), .in25(a0), .in26(a0), .in27(a0),
    .in28(a0), .in29(a0), .in30(a0), .in31(a0), .out(multiplexer_8_out), .sel(WriteIndex));
  Register #(.width(32)) register_6 (.D(multiplexer_6_out), .en(RegWEn), .clk(clk), .Q(s0));  // open: clr
  Register #(.width(32)) register_7 (.D(multiplexer_7_out), .en(RegWEn), .clk(clk), .Q(s1));  // open: clr
  Register #(.width(32)) register_8 (.D(multiplexer_8_out), .en(RegWEn), .clk(clk), .Q(a0));  // open: clr
  Multiplexer #(.select(5), .width(32)) multiplexer_9 (
    .in0({32{1'b0}}), .in1(ra), .in2(sp), .in3(gp), .in4(tp), .in5(t0), .in6(t1), .in7(t2), .in8(s0),
    .in9(s1), .in10(a0), .in11(a1), .in12(a2), .in13(a3), .in14(a4), .in15(a5), .in16(a6), .in17(a7),
    .in18(s2), .in19(s3), .in20(s4), .in21(s5), .in22(s6), .in23(s7), .in24(s8), .in25(s9), .in26(s10),
    .in27(s11), .in28(t3), .in29(t4), .in30(t5), .in31(t6), .out(ReadData1), .sel(ReadIndex1));
  Multiplexer #(.select(5), .width(32)) multiplexer_10 (
    .in0({32{1'b0}}), .in1(ra), .in2(sp), .in3(gp), .in4(tp), .in5(t0), .in6(t1), .in7(t2), .in8(s0),
    .in9(s1), .in10(a0), .in11(a1), .in12(a2), .in13(a3), .in14(a4), .in15(a5), .in16(a6), .in17(a7),
    .in18(s2), .in19(s3), .in20(s4), .in21(s5), .in22(s6), .in23(s7), .in24(s8), .in25(s9), .in26(s10),
    .in27(s11), .in28(t3), .in29(t4), .in30(t5), .in31(t6), .out(ReadData2), .sel(ReadIndex2));
  Multiplexer #(.select(5), .width(32)) multiplexer_11 (
    .in0(a1), .in1(a1), .in2(a1), .in3(a1), .in4(a1), .in5(a1), .in6(a1), .in7(a1), .in8(a1), .in9(a1),
    .in10(a1), .in11(WriteData), .in12(a1), .in13(a1), .in14(a1), .in15(a1), .in16(a1), .in17(a1), .in18(a1),
    .in19(a1), .in20(a1), .in21(a1), .in22(a1), .in23(a1), .in24(a1), .in25(a1), .in26(a1), .in27(a1),
    .in28(a1), .in29(a1), .in30(a1), .in31(a1), .out(multiplexer_11_out), .sel(WriteIndex));
  Register #(.width(32)) register_9 (.D(multiplexer_11_out), .en(RegWEn), .clk(clk), .Q(a1));  // open: clr
  Multiplexer #(.select(5), .width(32)) multiplexer_12 (
    .in0(gp), .in1(gp), .in2(gp), .in3(WriteData), .in4(gp), .in5(gp), .in6(gp), .in7(gp), .in8(gp),
    .in9(gp), .in10(gp), .in11(gp), .in12(gp), .in13(gp), .in14(gp), .in15(gp), .in16(gp), .in17(gp),
    .in18(gp), .in19(gp), .in20(gp), .in21(gp), .in22(gp), .in23(gp), .in24(gp), .in25(gp), .in26(gp),
    .in27(gp), .in28(gp), .in29(gp), .in30(gp), .in31(gp), .out(multiplexer_12_out), .sel(WriteIndex));
  Register #(.width(32)) register_10 (.D(multiplexer_12_out), .en(RegWEn), .clk(clk), .Q(gp));  // open: clr
  Multiplexer #(.select(5), .width(32)) multiplexer_13 (
    .in0(s9), .in1(s9), .in2(s9), .in3(s9), .in4(s9), .in5(s9), .in6(s9), .in7(s9), .in8(s9), .in9(s9),
    .in10(s9), .in11(s9), .in12(s9), .in13(s9), .in14(s9), .in15(s9), .in16(s9), .in17(s9), .in18(s9),
    .in19(s9), .in20(s9), .in21(s9), .in22(s9), .in23(s9), .in24(s9), .in25(WriteData), .in26(s9), .in27(s9),
    .in28(s9), .in29(s9), .in30(s9), .in31(s9), .out(multiplexer_13_out), .sel(WriteIndex));
  Register #(.width(32)) register_11 (.D(multiplexer_13_out), .en(RegWEn), .clk(clk), .Q(s9));  // open: clr
  Multiplexer #(.select(5), .width(32)) multiplexer_14 (
    .in0(a2), .in1(a2), .in2(a2), .in3(a2), .in4(a2), .in5(a2), .in6(a2), .in7(a2), .in8(a2), .in9(a2),
    .in10(a2), .in11(a2), .in12(WriteData), .in13(a2), .in14(a2), .in15(a2), .in16(a2), .in17(a2), .in18(a2),
    .in19(a2), .in20(a2), .in21(a2), .in22(a2), .in23(a2), .in24(a2), .in25(a2), .in26(a2), .in27(a2),
    .in28(a2), .in29(a2), .in30(a2), .in31(a2), .out(multiplexer_14_out), .sel(WriteIndex));
  Register #(.width(32)) register_12 (.D(multiplexer_14_out), .en(RegWEn), .clk(clk), .Q(a2));  // open: clr
  Multiplexer #(.select(5), .width(32)) multiplexer_15 (
    .in0(tp), .in1(tp), .in2(tp), .in3(tp), .in4(WriteData), .in5(tp), .in6(tp), .in7(tp), .in8(tp),
    .in9(tp), .in10(tp), .in11(tp), .in12(tp), .in13(tp), .in14(tp), .in15(tp), .in16(tp), .in17(tp),
    .in18(tp), .in19(tp), .in20(tp), .in21(tp), .in22(tp), .in23(tp), .in24(tp), .in25(tp), .in26(tp),
    .in27(tp), .in28(tp), .in29(tp), .in30(tp), .in31(tp), .out(multiplexer_15_out), .sel(WriteIndex));
  Register #(.width(32)) register_13 (.D(multiplexer_15_out), .en(RegWEn), .clk(clk), .Q(tp));  // open: clr
  Multiplexer #(.select(5), .width(32)) multiplexer_16 (
    .in0(s10), .in1(s10), .in2(s10), .in3(s10), .in4(s10), .in5(s10), .in6(s10), .in7(s10), .in8(s10),
    .in9(s10), .in10(s10), .in11(s10), .in12(s10), .in13(s10), .in14(s10), .in15(s10), .in16(s10),
    .in17(s10), .in18(s10), .in19(s10), .in20(s10), .in21(s10), .in22(s10), .in23(s10), .in24(s10),
    .in25(s10), .in26(WriteData), .in27(s10), .in28(s10), .in29(s10), .in30(s10), .in31(s10),
    .out(multiplexer_16_out), .sel(WriteIndex));
  Multiplexer #(.select(5), .width(32)) multiplexer_17 (
    .in0(a3), .in1(a3), .in2(a3), .in3(a3), .in4(a3), .in5(a3), .in6(a3), .in7(a3), .in8(a3), .in9(a3),
    .in10(a3), .in11(a3), .in12(a3), .in13(WriteData), .in14(a3), .in15(a3), .in16(a3), .in17(a3), .in18(a3),
    .in19(a3), .in20(a3), .in21(a3), .in22(a3), .in23(a3), .in24(a3), .in25(a3), .in26(a3), .in27(a3),
    .in28(a3), .in29(a3), .in30(a3), .in31(a3), .out(multiplexer_17_out), .sel(WriteIndex));
  Register #(.width(32)) register_14 (.D(multiplexer_16_out), .en(RegWEn), .clk(clk), .Q(s10));  // open: clr
  Register #(.width(32)) register_15 (.D(multiplexer_17_out), .en(RegWEn), .clk(clk), .Q(a3));  // open: clr
  Multiplexer #(.select(5), .width(32)) multiplexer_18 (
    .in0(s3), .in1(s3), .in2(s3), .in3(s3), .in4(s3), .in5(s3), .in6(s3), .in7(s3), .in8(s3), .in9(s3),
    .in10(s3), .in11(s3), .in12(s3), .in13(s3), .in14(s3), .in15(s3), .in16(s3), .in17(s3), .in18(s3),
    .in19(WriteData), .in20(s3), .in21(s3), .in22(s3), .in23(s3), .in24(s3), .in25(s3), .in26(s3), .in27(s3),
    .in28(s3), .in29(s3), .in30(s3), .in31(s3), .out(multiplexer_18_out), .sel(WriteIndex));
  Register #(.width(32)) register_16 (.D(multiplexer_18_out), .en(RegWEn), .clk(clk), .Q(s3));  // open: clr
  Multiplexer #(.select(5), .width(32)) multiplexer_19 (
    .in0(s11), .in1(s11), .in2(s11), .in3(s11), .in4(s11), .in5(s11), .in6(s11), .in7(s11), .in8(s11),
    .in9(s11), .in10(s11), .in11(s11), .in12(s11), .in13(s11), .in14(s11), .in15(s11), .in16(s11),
    .in17(s11), .in18(s11), .in19(s11), .in20(s11), .in21(s11), .in22(s11), .in23(s11), .in24(s11),
    .in25(s11), .in26(s11), .in27(WriteData), .in28(s11), .in29(s11), .in30(s11), .in31(s11),
    .out(multiplexer_19_out), .sel(WriteIndex));
  Multiplexer #(.select(5), .width(32)) multiplexer_20 (
    .in0(a4), .in1(a4), .in2(a4), .in3(a4), .in4(a4), .in5(a4), .in6(a4), .in7(a4), .in8(a4), .in9(a4),
    .in10(a4), .in11(a4), .in12(a4), .in13(a4), .in14(WriteData), .in15(a4), .in16(a4), .in17(a4), .in18(a4),
    .in19(a4), .in20(a4), .in21(a4), .in22(a4), .in23(a4), .in24(a4), .in25(a4), .in26(a4), .in27(a4),
    .in28(a4), .in29(a4), .in30(a4), .in31(a4), .out(multiplexer_20_out), .sel(WriteIndex));
  Register #(.width(32)) register_17 (.D(multiplexer_19_out), .en(RegWEn), .clk(clk), .Q(s11));  // open: clr
  Register #(.width(32)) register_18 (.D(multiplexer_20_out), .en(RegWEn), .clk(clk), .Q(a4));  // open: clr
  Multiplexer #(.select(5), .width(32)) multiplexer_21 (
    .in0(s4), .in1(s4), .in2(s4), .in3(s4), .in4(s4), .in5(s4), .in6(s4), .in7(s4), .in8(s4), .in9(s4),
    .in10(s4), .in11(s4), .in12(s4), .in13(s4), .in14(s4), .in15(s4), .in16(s4), .in17(s4), .in18(s4),
    .in19(s4), .in20(WriteData), .in21(s4), .in22(s4), .in23(s4), .in24(s4), .in25(s4), .in26(s4), .in27(s4),
    .in28(s4), .in29(s4), .in30(s4), .in31(s4), .out(multiplexer_21_out), .sel(WriteIndex));
  Register #(.width(32)) register_19 (.D(multiplexer_21_out), .en(RegWEn), .clk(clk), .Q(s4));  // open: clr
  Multiplexer #(.select(5), .width(32)) multiplexer_22 (
    .in0(a5), .in1(a5), .in2(a5), .in3(a5), .in4(a5), .in5(a5), .in6(a5), .in7(a5), .in8(a5), .in9(a5),
    .in10(a5), .in11(a5), .in12(a5), .in13(a5), .in14(a5), .in15(WriteData), .in16(a5), .in17(a5), .in18(a5),
    .in19(a5), .in20(a5), .in21(a5), .in22(a5), .in23(a5), .in24(a5), .in25(a5), .in26(a5), .in27(a5),
    .in28(a5), .in29(a5), .in30(a5), .in31(a5), .out(multiplexer_22_out), .sel(WriteIndex));
  Multiplexer #(.select(5), .width(32)) multiplexer_23 (
    .in0(t3), .in1(t3), .in2(t3), .in3(t3), .in4(t3), .in5(t3), .in6(t3), .in7(t3), .in8(t3), .in9(t3),
    .in10(t3), .in11(t3), .in12(t3), .in13(t3), .in14(t3), .in15(t3), .in16(t3), .in17(t3), .in18(t3),
    .in19(t3), .in20(t3), .in21(t3), .in22(t3), .in23(t3), .in24(t3), .in25(t3), .in26(t3), .in27(t3),
    .in28(WriteData), .in29(t3), .in30(t3), .in31(t3), .out(multiplexer_23_out), .sel(WriteIndex));
  Register #(.width(32)) register_20 (.D(multiplexer_23_out), .en(RegWEn), .clk(clk), .Q(t3));  // open: clr
  Register #(.width(32)) register_21 (.D(multiplexer_22_out), .en(RegWEn), .clk(clk), .Q(a5));  // open: clr
  Multiplexer #(.select(5), .width(32)) multiplexer_24 (
    .in0(s5), .in1(s5), .in2(s5), .in3(s5), .in4(s5), .in5(s5), .in6(s5), .in7(s5), .in8(s5), .in9(s5),
    .in10(s5), .in11(s5), .in12(s5), .in13(s5), .in14(s5), .in15(s5), .in16(s5), .in17(s5), .in18(s5),
    .in19(s5), .in20(s5), .in21(WriteData), .in22(s5), .in23(s5), .in24(s5), .in25(s5), .in26(s5), .in27(s5),
    .in28(s5), .in29(s5), .in30(s5), .in31(s5), .out(multiplexer_24_out), .sel(WriteIndex));
  Register #(.width(32)) register_22 (.D(multiplexer_24_out), .en(RegWEn), .clk(clk), .Q(s5));  // open: clr
  Multiplexer #(.select(5), .width(32)) multiplexer_25 (
    .in0(a6), .in1(a6), .in2(a6), .in3(a6), .in4(a6), .in5(a6), .in6(a6), .in7(a6), .in8(a6), .in9(a6),
    .in10(a6), .in11(a6), .in12(a6), .in13(a6), .in14(a6), .in15(a6), .in16(WriteData), .in17(a6), .in18(a6),
    .in19(a6), .in20(a6), .in21(a6), .in22(a6), .in23(a6), .in24(a6), .in25(a6), .in26(a6), .in27(a6),
    .in28(a6), .in29(a6), .in30(a6), .in31(a6), .out(multiplexer_25_out), .sel(WriteIndex));
  Multiplexer #(.select(5), .width(32)) multiplexer_26 (
    .in0(t4), .in1(t4), .in2(t4), .in3(t4), .in4(t4), .in5(t4), .in6(t4), .in7(t4), .in8(t4), .in9(t4),
    .in10(t4), .in11(t4), .in12(t4), .in13(t4), .in14(t4), .in15(t4), .in16(t4), .in17(t4), .in18(t4),
    .in19(t4), .in20(t4), .in21(t4), .in22(t4), .in23(t4), .in24(t4), .in25(t4), .in26(t4), .in27(t4),
    .in28(t4), .in29(WriteData), .in30(t4), .in31(t4), .out(multiplexer_26_out), .sel(WriteIndex));
  Register #(.width(32)) register_23 (.D(multiplexer_26_out), .en(RegWEn), .clk(clk), .Q(t4));  // open: clr
  Register #(.width(32)) register_24 (.D(multiplexer_25_out), .en(RegWEn), .clk(clk), .Q(a6));  // open: clr
  Multiplexer #(.select(5), .width(32)) multiplexer_27 (
    .in0(s6), .in1(s6), .in2(s6), .in3(s6), .in4(s6), .in5(s6), .in6(s6), .in7(s6), .in8(s6), .in9(s6),
    .in10(s6), .in11(s6), .in12(s6), .in13(s6), .in14(s6), .in15(s6), .in16(s6), .in17(s6), .in18(s6),
    .in19(s6), .in20(s6), .in21(s6), .in22(WriteData), .in23(s6), .in24(s6), .in25(s6), .in26(s6), .in27(s6),
    .in28(s6), .in29(s6), .in30(s6), .in31(s6), .out(multiplexer_27_out), .sel(WriteIndex));
  Register #(.width(32)) register_25 (.D(multiplexer_27_out), .en(RegWEn), .clk(clk), .Q(s6));  // open: clr
  Multiplexer #(.select(5), .width(32)) multiplexer_28 (
    .in0(t5), .in1(t5), .in2(t5), .in3(t5), .in4(t5), .in5(t5), .in6(t5), .in7(t5), .in8(t5), .in9(t5),
    .in10(t5), .in11(t5), .in12(t5), .in13(t5), .in14(t5), .in15(t5), .in16(t5), .in17(t5), .in18(t5),
    .in19(t5), .in20(t5), .in21(t5), .in22(t5), .in23(t5), .in24(t5), .in25(t5), .in26(t5), .in27(t5),
    .in28(t5), .in29(t5), .in30(WriteData), .in31(t5), .out(multiplexer_28_out), .sel(WriteIndex));
  Multiplexer #(.select(5), .width(32)) multiplexer_29 (
    .in0(a7), .in1(a7), .in2(a7), .in3(a7), .in4(a7), .in5(a7), .in6(a7), .in7(a7), .in8(a7), .in9(a7),
    .in10(a7), .in11(a7), .in12(a7), .in13(a7), .in14(a7), .in15(a7), .in16(a7), .in17(WriteData), .in18(a7),
    .in19(a7), .in20(a7), .in21(a7), .in22(a7), .in23(a7), .in24(a7), .in25(a7), .in26(a7), .in27(a7),
    .in28(a7), .in29(a7), .in30(a7), .in31(a7), .out(multiplexer_29_out), .sel(WriteIndex));
  Register #(.width(32)) register_26 (.D(multiplexer_29_out), .en(RegWEn), .clk(clk), .Q(a7));  // open: clr
  Register #(.width(32)) register_27 (.D(multiplexer_28_out), .en(RegWEn), .clk(clk), .Q(t5));  // open: clr
  Multiplexer #(.select(5), .width(32)) multiplexer_30 (
    .in0(s7), .in1(s7), .in2(s7), .in3(s7), .in4(s7), .in5(s7), .in6(s7), .in7(s7), .in8(s7), .in9(s7),
    .in10(s7), .in11(s7), .in12(s7), .in13(s7), .in14(s7), .in15(s7), .in16(s7), .in17(s7), .in18(s7),
    .in19(s7), .in20(s7), .in21(s7), .in22(s7), .in23(WriteData), .in24(s7), .in25(s7), .in26(s7), .in27(s7),
    .in28(s7), .in29(s7), .in30(s7), .in31(s7), .out(multiplexer_30_out), .sel(WriteIndex));
  Register #(.width(32)) register_28 (.D(multiplexer_30_out), .en(RegWEn), .clk(clk), .Q(s7));  // open: clr
  Multiplexer #(.select(5), .width(32)) multiplexer_31 (
    .in0(t6), .in1(t6), .in2(t6), .in3(t6), .in4(t6), .in5(t6), .in6(t6), .in7(t6), .in8(t6), .in9(t6),
    .in10(t6), .in11(t6), .in12(t6), .in13(t6), .in14(t6), .in15(t6), .in16(t6), .in17(t6), .in18(t6),
    .in19(t6), .in20(t6), .in21(t6), .in22(t6), .in23(t6), .in24(t6), .in25(t6), .in26(t6), .in27(t6),
    .in28(t6), .in29(t6), .in30(t6), .in31(WriteData), .out(multiplexer_31_out), .sel(WriteIndex));
  Multiplexer #(.select(5), .width(32)) multiplexer_32 (
    .in0(s2), .in1(s2), .in2(s2), .in3(s2), .in4(s2), .in5(s2), .in6(s2), .in7(s2), .in8(s2), .in9(s2),
    .in10(s2), .in11(s2), .in12(s2), .in13(s2), .in14(s2), .in15(s2), .in16(s2), .in17(s2), .in18(WriteData),
    .in19(s2), .in20(s2), .in21(s2), .in22(s2), .in23(s2), .in24(s2), .in25(s2), .in26(s2), .in27(s2),
    .in28(s2), .in29(s2), .in30(s2), .in31(s2), .out(multiplexer_32_out), .sel(WriteIndex));
  Register #(.width(32)) register_29 (.D(multiplexer_32_out), .en(RegWEn), .clk(clk), .Q(s2));  // open: clr
  Register #(.width(32)) register_30 (.D(multiplexer_31_out), .en(RegWEn), .clk(clk), .Q(t6));  // open: clr
  Multiplexer #(.select(5), .width(32)) multiplexer_33 (
    .in0(s8), .in1(s8), .in2(s8), .in3(s8), .in4(s8), .in5(s8), .in6(s8), .in7(s8), .in8(s8), .in9(s8),
    .in10(s8), .in11(s8), .in12(s8), .in13(s8), .in14(s8), .in15(s8), .in16(s8), .in17(s8), .in18(s8),
    .in19(s8), .in20(s8), .in21(s8), .in22(s8), .in23(s8), .in24(WriteData), .in25(s8), .in26(s8), .in27(s8),
    .in28(s8), .in29(s8), .in30(s8), .in31(s8), .out(multiplexer_33_out), .sel(WriteIndex));
  Register #(.width(32)) register_31 (.D(multiplexer_33_out), .en(RegWEn), .clk(clk), .Q(s8));  // open: clr

  // Notes on the sheet:
  //   INPUTS to your circuit
  //   DON'T CHANGE THE LOCATIONS OF THE INPUTS AND OUTPUTS!
  //   These are DEBUG/TEST outputs from your circuit.
  //   OUTPUTS from your circuit
endmodule
